# Fritzing sketch sample-plan (saved by Fritzing 0.9.5d)
breadboards: 1

parts:
  U1 = ESP 32 DEVKIT DOIT
  Componente1 = Bluetooth HC-05 Macho
  R1 = Resistor [tolerance=±5% resistance=270 package=THT]
  R2 = Resistor [tolerance=±5% resistance=270 package=THT]
  R4 = Resistor [tolerance=±5% resistance=270 package=THT]
  SG2 = Buzzer 12mm [package=buzzer-ccv-kit]
  LED1 = RGB LED (com. anode, rbg) [package="5 mm [THT]"]
  R5 = Resistor [tolerance=±5% resistance=100 package=THT]
  R6 = Resistor [tolerance=±5% resistance=1000 package=THT]
  R7 = Resistor [tolerance=±5% resistance=1000 package=THT]

nets:
  N1: U1.D23, R5.Pin_0
  N2: U1.D22, U1.D18, U1.D5, U1.TX2, U1.D4, U1.D2, R1.Pin_0, R2.Pin_0, R4.Pin_0
  GND: U1.TX0, U1.GND, Componente1.GND, SG2.2, LED1.common_anode, R6.Pin_0, R7.Pin_0
  N3: U1.RX0, Componente1.TXD
  VIN: U1.VIN, Componente1.VCC
  N4: Componente1.RXD, R6.Pin_1
  N5: R1.Pin_1, LED1.green_cathode
  N6: R2.Pin_1, LED1.blue_cathode
  N7: R4.Pin_1, LED1.red_cathode
  N8: SG2.1, R5.Pin_1
